# Fritzing sketch schematic (saved by Fritzing 0.9.3b)
breadboards: 1

parts:
  R = Resistor [tolerance=±5% resistance=9.1k package=THT]
  LED = LED - 3mm [color="Red (660nm)" package="3 mm [THT]"]

nets:
  5V: R.Pin_0
  N1: R.Pin_1, LED.anode
  GND: LED.cathode
