# Fritzing sketch schematic (saved by Fritzing 0.9.3b)
breadboards: 1

parts:
  R = Resistor [tolerance=±5% resistance=9.1k package=THT]
  LED = LED - 3mm [color="Red (660nm)" package="3 mm [THT]"]
  Button = Momentary Switch [package=tactile-pth]
  Part1 = Arduino Uno (Rev3)
  Power = DC Power [voltage=5V frequency=60]

nets:
  GND: R.Pin_1, LED.cathode, Power.V-
  N1: LED.anode, Part1.D13/SCK
  N2: Button.1, Part1.D2
  N3: Button.3, Power.V+
